# Fritzing sketch bb01v01 (saved by Fritzing 0.9.3b)
circuit board: 5cm x 3.5cm
breadboards: 1

parts:
  BATT1 = 3xAAA Switchable Battery Pack w/Bare Wire
  S2 = Pushbutton [package="[THT]"]
  S1 = Pushbutton [package="[THT]"]
  J1 = JST-VHR-3N [part_number=JST-VHR-3N package=THT]
  C1 = Electrolytic Capacitor [capacitance=1mF package="200 mil [THT, electrolytic]"]
  R2 = Resistor [tolerance=±5% resistance=10k package=THT]
  R3 = Resistor [tolerance=±5% resistance=10 package=THT]
  R1 = Resistor [tolerance=±5% resistance=470 package=THT]
  U1 = Adafruit Trinket 5V

nets (from the pcb view):
  N1: BATT1.POS, J1.pin1, J1.pin_4, C1.-, U1.VBAT
  N2: BATT1.NEG, J1.pin3, J1.pin_6, C1.+, R2.Pin_0, R3.Pin_0, U1.GND
  N3: S2.Pin_1, S2.Pin_2, R2.Pin_1, U1.#1
  N4: S2.Pin_3, S2.Pin_4, S1.Pin_1, S1.Pin_2, U1.+5V
  N5: S1.Pin_3, S1.Pin_4, R3.Pin_1, U1.#2
  N6: J1.pin2, J1.pin_5, R1.Pin_0
  N7: R1.Pin_1, U1.#0

custom parts:
  3xAAA Switchable Battery Pack w/Bare Wire: 3xAAA Switchable Battery Pack w/Bare Wire Connectors
  Adafruit Trinket 5V: Trinket may be small, but do not be fooled by its size! It's a tiny microcontroller board, built around the Atmel ATtiny85, a little chip with a lot of power. We wanted to design a microcontroller board that was small enough to fit into any project, and low cost enough to use without hesitation. Perfect for when you don't want to give up your expensive dev-board and you aren't willing to take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
